# Fritzing sketch Feather-System-w-LCD (saved by Fritzing 0.9.3b)

parts:
  Part2 = Adafruit Precision RTC FeatherWing [part_number="Adafruit #3028"]
  Part4 = Adafruit PowerRelay Feather Wing [part_number="Adafruit #3191"]
  Part5 = Adafruit Feather 32u4 Basic Proto [part_number="Adafruit #2771"]
  S1 = Pushbutton [package="[SMD]"]
  R1 = Resistor [tolerance=±5% resistance=10k package="0805 [SMD]"]
  Part6 = Adafruit I2C+SPI LCD Backpack [part_number="Adafruit #292"]

nets:
  GND: Part2.GND, Part4.GND, Part5.GND, R1.Pin_1, Part6.GND
  3.3V: Part2.3.3V, Part4.3.3V, Part5.+3V3, Part5.N$45, Part5.N$48, S1.Pin_3, S1.Pin_4
  N1: Part2.SDA, Part4.SDA, Part5.2, Part6.DATA
  N2: Part2.SCL, Part4.SCL, Part5.3, Part6.CLOCK
  N3: Part4.SCK, Part5.10
  N4: Part5.VBUS, Part6.VCC
  N5: Part5.9, Part5.N$18, Part5.N$43, S1.Pin_1, S1.Pin_2, R1.Pin_0

custom parts:
  Adafruit Precision RTC FeatherWing: A Feather board without ambition is a Feather board without FeatherWings! This is the DS3231 Precision RTC FeatherWing: it adds an extremely accurate I2C-integrated Real Time Clock (RTC) with a Temperature Compensated Crystal Oscillator (TCXO) to any Feather main board. This RTC is the most precise you can get in a small, low power package. Using our Feather Stacking Headers or Feather Female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
  Adafruit PowerRelay Feather Wing: A Feather board without ambition is a Feather board without FeatherWings! This is the Power Relay FeatherWing. It gives you power to control, and control over power. Put simply, you can now turn on and off lamps, fans, solenoids, and other small appliances that run on up to 250VAC or DC power using any Feather board. Compared to our smaller Relay FeatherWings, this one can handle a beefy 1200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
  Adafruit Feather 32u4 Basic Proto: At the Feather 32u4's heart is at ATmega32u4 clocked at 8 MHz and at 3.3V logic, a chip setup we've had tons of experience with as it's the same as the Flora. This chip has 32K of flash and 2K of RAM, with built in USB so not only does it have a USB-to-Serial program & debug capability built in with no need for an FTDI-like chip, it can also act like a mouse, keyboard, USB MIDI device, etc.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
  Adafruit I2C+SPI LCD Backpack: LCD backpacks reduce the number of pins needed to connect to an LCD. LCDs are a fun and easy way to have your microcontroller project talk back to you. Character LCDs are common, and easy to get, available in tons of colors and sizes. We've written tutorials on using character LCDs with an Arduino (or similar microcontroller) but find that the number of pins necessary to control the LCD can be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
