# Fritzing sketch 25 (saved by Fritzing 0.9.3b)
breadboards: 2

parts:
  Part1 = Adafruit I2C+SPI LCD Backpack [part_number="Adafruit #292"]
  Part2 = Arduino Uno (Rev3)
  Part3 = Adafruit PowerRelay Feather Wing [part_number="Adafruit #3191"]
  U1 = Optocoupler [package=THT]
  R1 = Resistor [tolerance=±5% resistance=220 package="2010 [SMD]"]
  S1 = Pushbutton [package="[THT]"]
  S2 = Toggle Switch [package=THT]
  S3 = Pushbutton [package="[THT]"]
  S4 = Pushbutton [package="[THT]"]
  S5 = Pushbutton [package="[THT]"]
  S6 = Pushbutton [package="[THT]"]
  S7 = Pushbutton [package="[THT]"]
  S8 = Pushbutton [package="[THT]"]
  R2 = Resistor [tolerance=±5% resistance=10k package="1206 [SMD]"]
  R3 = Resistor [tolerance=±5% resistance=10k package="1206 [SMD]"]
  R4 = Resistor [tolerance=±5% resistance=10k package="1206 [SMD]"]
  R5 = Resistor [tolerance=±5% resistance=10k package="1206 [SMD]"]
  R6 = Resistor [tolerance=±5% resistance=10k package="1206 [SMD]"]
  R7 = Resistor [tolerance=±5% resistance=10k package="1206 [SMD]"]
  R8 = Resistor [tolerance=±5% resistance=10k package="1206 [SMD]"]
  R9 = Resistor [tolerance=±5% resistance=10k package="1206 [SMD]"]

nets:
  GND: Part1.GND, Part2.GND, Part3.GND, U1.Pin_2, R2.Pin_1, R3.Pin_1, R4.Pin_1, R5.Pin_1, R6.Pin_1, R7.Pin_1, R8.Pin_1, R9.Pin_1
  VCC: Part1.VCC, Part2.5V, S1.Pin_3, S1.Pin_4, S2.L1, S3.Pin_3, S3.Pin_4, S4.Pin_3, S4.Pin_4, S5.Pin_3, S5.Pin_4, S6.Pin_3, S6.Pin_4, S7.Pin_3, S7.Pin_4, S8.Pin_3, S8.Pin_4
  N1: Part1.CLOCK, Part2.A4/SDA
  N2: Part1.DATA, Part2.A5/SCL
  N3: Part2.D8, S6.Pin_1, S6.Pin_2, R5.Pin_0
  N4: Part2.D9_PWM, S5.Pin_1, S5.Pin_2, R6.Pin_0
  N5: Part2.D10_PWM/SS, S8.Pin_1, S8.Pin_2, R8.Pin_0
  N6: Part2.D11_PWM/MOSI, S7.Pin_1, S7.Pin_2, R7.Pin_0
  N7: Part2.D3_PWM, R1.Pin_1
  N8: Part2.D4, S2.L2, R9.Pin_0
  N9: Part2.D5_PWM, S1.Pin_1, S1.Pin_2, R2.Pin_0
  N10: Part2.D6_PWM, S3.Pin_1, S3.Pin_2, R3.Pin_0
  N11: Part2.D7, S4.Pin_1, S4.Pin_2, R4.Pin_0
  3V3: Part2.3V3, Part3.3.3V, Part3.F, U1.Pin_6
  N12: Part3.SCK, U1.Pin_5
  N13: Part3.MOSI, U1.Pin_4
  N14: U1.Pin_1, R1.Pin_0

custom parts:
  Adafruit I2C+SPI LCD Backpack: LCD backpacks reduce the number of pins needed to connect to an LCD. LCDs are a fun and easy way to have your microcontroller project talk back to you. Character LCDs are common, and easy to get, available in tons of colors and sizes. We've written tutorials on using character LCDs with an Arduino (or similar microcontroller) but find that the number of pins necessary to control the LCD can be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
  Adafruit PowerRelay Feather Wing: A Feather board without ambition is a Feather board without FeatherWings! This is the Power Relay FeatherWing. It gives you power to control, and control over power. Put simply, you can now turn on and off lamps, fans, solenoids, and other small appliances that run on up to 250VAC or DC power using any Feather board. Compared to our smaller Relay FeatherWings, this one can handle a beefy 1200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

// code stored in the sketch: Relay_Circuit_as_of_5:25.ino

