# Fritzing sketch Trinket-Conditions-Monitor copy (saved by Fritzing 0.9.3b)
breadboards: 1

parts:
  Part2 = Adafruit Trinket 5V
  DHT1 = DHT22 Humidity and Temperature Sensor
  Part3 = Adafruit I2C+SPI LCD Backpack [part_number="Adafruit #292"]
  U1 = LCD-16X2 [package=lcd-16x2]
  R1 = Resistor [tolerance=±5% resistance=1k package=THT]

nets:
  GND: Part2.GND, DHT1.GND, Part3.GND, U1.DB5, U1.K
  N1: Part2.#1, DHT1.DATA, R1.Pin_1
  N2: Part2.#2, Part3.CLOCK
  N3: Part2.#0, Part3.DATA
  VDD: Part2.+5V, DHT1.VDD, Part3.VCC, U1.VDD, U1.A, R1.Pin_0
  N4: Part3.CONTRAST, U1.DB7
  N5: Part3.RS, U1.DB6
  N6: Part3.E, U1.DB4
  N7: Part3.DB0, U1.DB3
  N8: Part3.DB1, U1.DB2
  N9: Part3.DB2, U1.DB1
  N10: Part3.DB3, U1.DB0
  N11: Part3.DB4, U1.E
  N12: Part3.DB5, U1.R_W
  N13: Part3.DB6, U1.RS
  N14: Part3.DB7, U1.VO
  N15: Part3.LEDK, U1.VSS

custom parts:
  Adafruit Trinket 5V: Trinket may be small, but do not be fooled by its size! It's a tiny microcontroller board, built around the Atmel ATtiny85, a little chip with a lot of power. We wanted to design a microcontroller board that was small enough to fit into any project, and low cost enough to use without hesitation. Perfect for when you don't want to give up your expensive dev-board and you aren't willing to take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
  Adafruit I2C+SPI LCD Backpack: LCD backpacks reduce the number of pins needed to connect to an LCD. LCDs are a fun and easy way to have your microcontroller project talk back to you. Character LCDs are common, and easy to get, available in tons of colors and sizes. We've written tutorials on using character LCDs with an Arduino (or similar microcontroller) but find that the number of pins necessary to control the LCD can be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
