# Fritzing sketch relay_layout (saved by Fritzing 0.9.3b)
breadboards: 2

parts:
  Part1 = Adafruit PowerRelay Feather Wing [part_number="Adafruit #3191"]
  Part2 = Arduino Uno (Rev3)
  S2 = Pushbutton [package="[THT]"]
  S3 = Pushbutton [package="[THT]"]
  S4 = Pushbutton [package="[THT]"]
  S5 = Pushbutton [package="[THT]"]
  S6 = Pushbutton [package="[THT]"]
  S7 = Pushbutton [package="[THT]"]
  S8 = Pushbutton [package="[THT]"]
  S9 = Toggle Switch [package=THT]
  R1 = Resistor [tolerance=±5% resistance=10k package="0603 [SMD]"]
  R2 = Resistor [tolerance=±5% resistance=10k package="0603 [SMD]"]
  R3 = Resistor [tolerance=±5% resistance=10k package="0603 [SMD]"]
  R4 = Resistor [tolerance=±5% resistance=10k package="0603 [SMD]"]
  R5 = Resistor [tolerance=±5% resistance=10k package="0603 [SMD]"]
  R6 = Resistor [tolerance=±5% resistance=10k package="0603 [SMD]"]
  R7 = Resistor [tolerance=±5% resistance=10k package="0603 [SMD]"]
  R8 = Resistor [tolerance=±5% resistance=10k package="0603 [SMD]"]
  Part3 = Adafruit I2C+SPI LCD Backpack [part_number="Adafruit #292"]
  U1 = Optocoupler [package=THT]
  R9 = Resistor [tolerance=±5% resistance=220 package="0603 [SMD]"]

nets:
  3.3V: Part1.3.3V, Part1.SCK, Part2.3V3, U1.Pin_6
  GND: Part1.GND, Part2.GND, Part3.GND, U1.Pin_2
  N1: Part1.MOSI, U1.Pin_5
  N2: Part1.MISO, U1.Pin_4
  N3: Part2.A4/SDA, Part3.CLOCK
  N4: Part2.A5/SCL, Part3.DATA
  N5: Part2.D8, S5.Pin_1, S5.Pin_2, R5.Pin_0
  N6: Part2.D9_PWM, S6.Pin_1, S6.Pin_2, R6.Pin_0
  N7: Part2.D10_PWM/SS, S7.Pin_1, S7.Pin_2, R7.Pin_0
  N8: Part2.D11_PWM/MOSI, S8.Pin_1, S8.Pin_2, R8.Pin_0
  N9: Part2.D3_PWM, R9.Pin_1
  N10: Part2.D4, S9.COM, R1.Pin_0
  N11: Part2.D5_PWM, S2.Pin_1, S2.Pin_2, R4.Pin_0
  N12: Part2.D6_PWM, S3.Pin_1, S3.Pin_2, R3.Pin_0
  N13: Part2.D7, S4.Pin_1, S4.Pin_2
  5V: Part2.5V, S2.Pin_3, S2.Pin_4, S3.Pin_3, S3.Pin_4, S4.Pin_3, S4.Pin_4, S5.Pin_3, S5.Pin_4, S6.Pin_3, S6.Pin_4, S7.Pin_3, S7.Pin_4, S8.Pin_3, S8.Pin_4, S9.L1, R1.Pin_1, R2.Pin_1, R4.Pin_1, R5.Pin_1, R6.Pin_1, R7.Pin_1, R8.Pin_1, Part3.VCC
  N14: U1.Pin_1, R9.Pin_0

custom parts:
  Adafruit PowerRelay Feather Wing: A Feather board without ambition is a Feather board without FeatherWings! This is the Power Relay FeatherWing. It gives you power to control, and control over power. Put simply, you can now turn on and off lamps, fans, solenoids, and other small appliances that run on up to 250VAC or DC power using any Feather board. Compared to our smaller Relay FeatherWings, this one can handle a beefy 1200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
  Adafruit I2C+SPI LCD Backpack: LCD backpacks reduce the number of pins needed to connect to an LCD. LCDs are a fun and easy way to have your microcontroller project talk back to you. Character LCDs are common, and easy to get, available in tons of colors and sizes. We've written tutorials on using character LCDs with an Arduino (or similar microcontroller) but find that the number of pins necessary to control the LCD can be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
